# Fritzing sketch Oyster-schema (saved by Fritzing 0.9.3b)
breadboards: 1

parts:
  Componente1 = Arduino Uno (Rev3) - ICSP
  Q2 = NPN-Transistor [part_number=to-126 package="SOT-23 [SMD]"]
  R1 = Resistor [tolerance=±1% resistance=100 package="0402 [SMD]"]
  R3 = Resistor [tolerance=±1% resistance=100 package="0402 [SMD]"]
  R4 = Resistor [tolerance=±1% resistance=100 package="0402 [SMD]"]
  R5 = Resistor [tolerance=±1% resistance=100 package="0402 [SMD]"]
  R6 = Resistor [tolerance=±1% resistance=100 package="0402 [SMD]"]
  D1 = LTE-302 [package=lte-302]
  D2 = LTE-302 [package=lte-302]
  D3 = LTE-302 [package=lte-302]
  D4 = LTE-302 [package=lte-302]
  hc-sr1 = hc-sr04
  hc-sr2 = hc-sr04
  hc-sr3 = hc-sr04
  J1 = Basic Servo
  J2 = Basic Servo
  U1 = LIPO-1000mAh [package=lipo-1000]
  U2 = SWITCH-SPST-2 [package=r_sw_th]
  IC1 = Voltage Regulator [package=to220-igo]
  C1 = Electrolytic Capacitor [capacitance=100nF voltage=20V package="300 mil [THT, electrolytic]"]
  C4 = Capacitor Polarized [part_number="330 nF" package=panasonic_h13]

nets:
  VCC: Componente1.5V, R3.Pin_0, R4.Pin_0, R5.Pin_0, R6.Pin_0, hc-sr1.VCC, hc-sr2.VCC, hc-sr3.VCC
  GND: Componente1.GND, D1.C, D2.C, D4.C, hc-sr1.GND, hc-sr2.GND, hc-sr3.GND
  N1: Componente1.D8, hc-sr2.Trig
  N2: Componente1.D9_PWM, J1.pulse
  N3: Componente1.D10_PWM/SS, J2.pulse
  N4: Componente1.D11_PWM/MOSI, hc-sr2.Echo
  N5: Componente1.D12/MISO, hc-sr3.Trig
  N6: Componente1.D13/SCK, hc-sr3.Echo
  N7: Componente1.D3_PWM, R1.Pin_0
  N8: Componente1.D6_PWM, hc-sr1.Trig
  N9: Componente1.D7, hc-sr1.Echo
  N10: Componente1.VIN, U2.P, IC1.IN, C4.+
  N11: Q2.2, D1.A, D2.A, D3.A, D4.A
  N12: Q2.0, R1.Pin_1
  N13: Q2.1, R3.Pin_1, R4.Pin_1, R5.Pin_1, R6.Pin_1
  GND_2: J1.gnd, J2.gnd, C1.-, C4.-
  VCC_2: J1.vcc, J2.vcc, IC1.OUT, C1.+
  N14: U1.+, U2.O
  N15: U1.-, IC1.GND
